// Logisim project All cases.circ as structural Verilog: 1 circuit, main circuit main
module main (
  input  [7:0] A,
  input  [7:0] B,
  input  Enable,
  input  Load,
  input  [1:0] C1_C0,
  input  Hold,
  output Q0,
  output Q1,
  output Q2,
  output Q3,
  output Q4,
  output Q5,
  output Q6,
  output Q7,
  output Q8,
  output Q9,
  output Q10,
  output Q11,
  output Q12,
  output Q13,
  output Q14,
  output Q15
);

  wire Clock_out;
  wire [15:0] bit_extender_1_out, main_1_q0, main_2_q0, main_3_q0, main_4_p17;

  case_01_main main_1 (
    .counter_Holder_H(Hold), .Clock(Clock_out), .Q0(main_1_q0[0]), .Q1(main_1_q0[1]), .Q2(main_1_q0[2]),
    .Q3(main_1_q0[3]), .Q4(main_1_q0[4]), .Q5(main_1_q0[5]), .Q6(main_1_q0[6]), .Q7(main_1_q0[7]),
    .Q8(main_1_q0[8]), .Q9(main_1_q0[9]), .Q10(main_1_q0[10]), .Q11(main_1_q0[11]), .Q12(main_1_q0[12]),
    .Q13(main_1_q0[13]), .Q14(main_1_q0[14]), .Q15(main_1_q0[15]), .Enable(Enable));
  case_00_main main_2 (
    .A8(A[0]), .A9(A[1]), .A10(A[2]), .A11(A[3]), .Q0(main_2_q0[0]), .Q1(main_2_q0[1]), .Q2(main_2_q0[2]),
    .Q3(main_2_q0[3]), .Q4(main_2_q0[4]), .Q5(main_2_q0[5]), .Q6(main_2_q0[6]), .Q7(main_2_q0[7]),
    .Enable(Enable), .A14(A[6]), .A7(B[7]), .A6(B[6]), .A5(B[5]), .A4(B[4]), .A3(B[3]), .A2(B[2]), .A1(B[1]),
    .A0(B[0]), .Q8(main_2_q0[8]), .Q9(main_2_q0[9]), .Q10(main_2_q0[10]), .Q11(main_2_q0[11]),
    .Q12(main_2_q0[12]), .Q13(main_2_q0[13]), .Q14(main_2_q0[14]), .Q15(main_2_q0[15]), .A12(A[4]),
    .A13(A[5]), .A15(A[7]));
  Clock Clock (.out(Clock_out));
  assign bit_extender_1_out = {{8{1'b0}}, A};  // Bit_Extender bit_extender_1
  case_10_main main_3 (
    .Load(Load), .Q0(main_3_q0[0]), .Q15(main_3_q0[15]), .Q14(main_3_q0[14]), .Q13(main_3_q0[13]),
    .Q12(main_3_q0[12]), .Q11(main_3_q0[11]), .Q10(main_3_q0[10]), .Q9(main_3_q0[9]), .Q8(main_3_q0[8]),
    .Q1(main_3_q0[1]), .Q2(main_3_q0[2]), .Q3(main_3_q0[3]), .Q4(main_3_q0[4]), .Q7(main_3_q0[7]),
    .Q6(main_3_q0[6]), .Q5(main_3_q0[5]), .A15(bit_extender_1_out[15]), .A14(bit_extender_1_out[14]),
    .A13(bit_extender_1_out[13]), .A12(bit_extender_1_out[12]), .A11(bit_extender_1_out[11]),
    .A10(bit_extender_1_out[10]), .A9(bit_extender_1_out[9]), .A8(bit_extender_1_out[8]),
    .A7(bit_extender_1_out[7]), .A6(bit_extender_1_out[6]), .A0(bit_extender_1_out[0]),
    .A1(bit_extender_1_out[1]), .A2(bit_extender_1_out[2]), .A4(bit_extender_1_out[4]),
    .A3(bit_extender_1_out[3]), .A5(bit_extender_1_out[5]), .B0(B[0]), .B1(B[1]), .B2(B[2]), .B3(B[3]),
    .B4(B[4]), .B5(B[5]), .B6(B[6]), .B7(B[7]), .Enable(Enable), .Clock(Clock_out));
  // Case_11_main main_4: pin names not known; wires that end beside it: B[0], B[1], B[2], B[3], B[4], B[5], B[6], B[7], A[0], A[1], A[2], A[3], A[4], A[5], A[6], A[7], main_4_p17[0], main_4_p17[1], main_4_p17[2], main_4_p17[3], main_4_p17[4], main_4_p17[5], main_4_p17[6], main_4_p17[7], main_4_p17[8], main_4_p17[9], main_4_p17[10], main_4_p17[11], main_4_p17[12], main_4_p17[13], main_4_p17[14], main_4_p17[15]
  Multiplexer #(.select(2), .width(16)) multiplexer_1 (
    .in0(main_2_q0), .in1(main_1_q0), .in2(main_3_q0), .in3(main_4_p17),
    .out({Q15, Q14, Q13, Q12, Q11, Q10, Q9, Q8, Q7, Q6, Q5, Q4, Q3, Q2, Q1, Q0}), .sel(C1_C0));  // open: en
endmodule
