// Logisim project Case 11.circ as structural Verilog: 1 circuit, main circuit main
module main (
  input  A0,
  input  A1,
  input  A2,
  input  A3,
  input  A4,
  input  A5,
  input  A6,
  input  A7,
  input  A8,
  input  A9,
  input  A10,
  input  A11,
  input  A12,
  input  A13,
  input  A14,
  input  A15,
  output Q8,
  output Q9,
  output Q10,
  output Q11,
  output Q12,
  output Q13,
  output Q14,
  output Q0,
  output Q1,
  output Q2,
  output Q3,
  output Q4,
  output Q5,
  output Q6,
  output Q7,
  output Q16
);

  xor odd_parity_1 (Q16, A0, A1, A2, A3, A4, A5, A6, A7);

  assign Q0 = A0;
  assign Q1 = A1;
  assign Q2 = A2;
  assign Q3 = A3;
  assign Q4 = A4;
  assign Q5 = A5;
  assign Q6 = A6;
  assign Q7 = A7;
  assign Q8 = 1'b0;
  assign Q9 = 1'b0;
  assign Q10 = 1'b0;
  assign Q11 = 1'b0;
  assign Q12 = 1'b0;
  assign Q13 = 1'b0;
  assign Q14 = 1'b0;
endmodule
