// Logisim project Product.circ as structural Verilog: 1 circuit, main circuit main
module main (
  input  A15,
  input  A14,
  input  A13,
  input  A12,
  input  A11,
  input  A10,
  input  A1,
  input  A9,
  input  A8,
  input  A6,
  input  A5,
  input  A3,
  input  A2,
  input  A0,
  input  A7,
  input  A4,
  input  Load,
  input  Enable,
  input  Clock,
  input  Reset,
  output Q15,
  output Q14,
  output Q13,
  output Q12,
  output Q11,
  output Q10,
  output Q9,
  output Q8,
  output Q7,
  output Q6,
  output Q5,
  output Q4,
  output Q3,
  output Q2,
  output Q1,
  output Q0
);

  wire multiplexer_1_out, multiplexer_2_out, multiplexer_3_out, multiplexer_4_out, multiplexer_5_out,
       multiplexer_6_out, multiplexer_7_out, multiplexer_8_out, multiplexer_9_out, multiplexer_10_out,
       multiplexer_11_out, multiplexer_12_out, multiplexer_13_out, multiplexer_14_out, multiplexer_15_out,
       multiplexer_16_out;

  Multiplexer multiplexer_1 (.in0(Q15), .in1(A15), .out(multiplexer_1_out), .sel(Load));  // open: en
  D_Flip_Flop d_ff_1 (.clk(Clock), .D(multiplexer_1_out), .Q(Q15), .en(Enable), .reset(Reset));  // open: Qn, preset
  Multiplexer multiplexer_2 (.in0(Q14), .in1(A14), .out(multiplexer_2_out), .sel(Load));  // open: en
  D_Flip_Flop d_ff_2 (.clk(Clock), .D(multiplexer_2_out), .Q(Q14), .en(Enable), .reset(Reset));  // open: Qn, preset
  Multiplexer multiplexer_3 (.in0(Q13), .in1(A13), .out(multiplexer_3_out), .sel(Load));  // open: en
  D_Flip_Flop d_ff_3 (.clk(Clock), .D(multiplexer_3_out), .Q(Q13), .en(Enable), .reset(Reset));  // open: Qn, preset
  Multiplexer multiplexer_4 (.in0(Q12), .in1(A12), .out(multiplexer_4_out), .sel(Load));  // open: en
  D_Flip_Flop d_ff_4 (.clk(Clock), .D(multiplexer_4_out), .Q(Q12), .en(Enable), .reset(Reset));  // open: Qn, preset
  Multiplexer multiplexer_5 (.in0(Q11), .in1(A11), .out(multiplexer_5_out), .sel(Load));  // open: en
  D_Flip_Flop d_ff_5 (.clk(Clock), .D(multiplexer_5_out), .Q(Q11), .en(Enable), .reset(Reset));  // open: Qn, preset
  Multiplexer multiplexer_6 (.in0(Q10), .in1(A10), .out(multiplexer_6_out), .sel(Load));  // open: en
  D_Flip_Flop d_ff_6 (.clk(Clock), .D(multiplexer_6_out), .Q(Q10), .en(Enable), .reset(Reset));  // open: Qn, preset
  Multiplexer multiplexer_7 (.in0(Q9), .in1(A9), .out(multiplexer_7_out), .sel(Load));  // open: en
  D_Flip_Flop d_ff_7 (.clk(Clock), .D(multiplexer_7_out), .Q(Q9), .en(Enable), .reset(Reset));  // open: Qn, preset
  Multiplexer multiplexer_8 (.in0(Q8), .in1(A8), .out(multiplexer_8_out), .sel(Load));  // open: en
  D_Flip_Flop d_ff_8 (.clk(Clock), .D(multiplexer_8_out), .Q(Q8), .en(Enable), .reset(Reset));  // open: Qn, preset
  Multiplexer multiplexer_9 (.in0(Q7), .in1(A7), .out(multiplexer_9_out), .sel(Load));  // open: en
  D_Flip_Flop d_ff_9 (.clk(Clock), .D(multiplexer_9_out), .Q(Q7), .en(Enable), .reset(Reset));  // open: Qn, preset
  Multiplexer multiplexer_10 (.in0(Q6), .in1(A6), .out(multiplexer_10_out), .sel(Load));  // open: en
  D_Flip_Flop d_ff_10 (.clk(Clock), .D(multiplexer_10_out), .Q(Q6), .en(Enable), .reset(Reset));  // open: Qn, preset
  Multiplexer multiplexer_11 (.in0(Q5), .in1(A5), .out(multiplexer_11_out), .sel(Load));  // open: en
  D_Flip_Flop d_ff_11 (.clk(Clock), .D(multiplexer_11_out), .Q(Q5), .en(Enable), .reset(Reset));  // open: Qn, preset
  Multiplexer multiplexer_12 (.in0(Q4), .in1(A4), .out(multiplexer_12_out), .sel(Load));  // open: en
  D_Flip_Flop d_ff_12 (.clk(Clock), .D(multiplexer_12_out), .Q(Q4), .en(Enable), .reset(Reset));  // open: Qn, preset
  Multiplexer multiplexer_13 (.in0(Q3), .in1(A3), .out(multiplexer_13_out), .sel(Load));  // open: en
  D_Flip_Flop d_ff_13 (.clk(Clock), .D(multiplexer_13_out), .Q(Q3), .en(Enable), .reset(Reset));  // open: Qn, preset
  Multiplexer multiplexer_14 (.in0(Q2), .in1(A2), .out(multiplexer_14_out), .sel(Load));  // open: en
  D_Flip_Flop d_ff_14 (.clk(Clock), .D(multiplexer_14_out), .Q(Q2), .en(Enable), .reset(Reset));  // open: Qn, preset
  Multiplexer multiplexer_15 (.in0(Q1), .in1(A1), .out(multiplexer_15_out), .sel(Load));  // open: en
  D_Flip_Flop d_ff_15 (.clk(Clock), .D(multiplexer_15_out), .Q(Q1), .en(Enable), .reset(Reset));  // open: Qn, preset
  Multiplexer multiplexer_16 (.in0(Q0), .in1(A0), .out(multiplexer_16_out), .sel(Load));  // open: en
  D_Flip_Flop d_ff_16 (.clk(Clock), .D(multiplexer_16_out), .Q(Q0), .en(Enable), .reset(Reset));  // open: Qn, preset
endmodule
