// Logisim project SR.circ as structural Verilog: 1 circuit, main circuit main
module main (
  input  B7,
  input  B6,
  input  B5,
  input  B4,
  input  B3,
  input  B2,
  input  B1,
  input  B0,
  input  Load,
  input  Clock,
  input  Enable,
  output Q7,
  output Q6,
  output Q5,
  output Q4,
  output Q3,
  output Q2,
  output Q1,
  output Q0
);

  wire multiplexer_1_out, multiplexer_2_out, multiplexer_3_out, multiplexer_4_out, multiplexer_5_out,
       multiplexer_6_out, multiplexer_7_out, multiplexer_8_out;

  Multiplexer multiplexer_1 (.in0(1'b0), .in1(B7), .out(multiplexer_1_out), .sel(Load));  // open: en
  Multiplexer multiplexer_2 (.in0(Q7), .in1(B6), .out(multiplexer_2_out), .sel(Load));  // open: en
  D_Flip_Flop d_ff_1 (.clk(Clock), .D(multiplexer_1_out), .Q(Q7), .en(Enable));  // open: Qn, preset, reset
  D_Flip_Flop d_ff_2 (.clk(Clock), .D(multiplexer_2_out), .Q(Q6), .en(Enable));  // open: Qn, preset, reset
  Multiplexer multiplexer_3 (.in0(Q6), .in1(B5), .out(multiplexer_3_out), .sel(Load));  // open: en
  D_Flip_Flop d_ff_3 (.clk(Clock), .D(multiplexer_3_out), .Q(Q5), .en(Enable));  // open: Qn, preset, reset
  Multiplexer multiplexer_4 (.in0(Q5), .in1(B4), .out(multiplexer_4_out), .sel(Load));  // open: en
  D_Flip_Flop d_ff_4 (.clk(Clock), .D(multiplexer_4_out), .Q(Q4), .en(Enable));  // open: Qn, preset, reset
  Multiplexer multiplexer_5 (.in0(Q4), .in1(B3), .out(multiplexer_5_out), .sel(Load));  // open: en
  D_Flip_Flop d_ff_5 (.clk(Clock), .D(multiplexer_5_out), .Q(Q3), .en(Enable));  // open: Qn, preset, reset
  Multiplexer multiplexer_6 (.in0(Q3), .in1(B2), .out(multiplexer_6_out), .sel(Load));  // open: en
  D_Flip_Flop d_ff_6 (.clk(Clock), .D(multiplexer_6_out), .Q(Q2), .en(Enable));  // open: Qn, preset, reset
  Multiplexer multiplexer_7 (.in0(Q2), .in1(B1), .out(multiplexer_7_out), .sel(Load));  // open: en
  D_Flip_Flop d_ff_7 (.clk(Clock), .D(multiplexer_7_out), .Q(Q1), .en(Enable));  // open: Qn, preset, reset
  Multiplexer multiplexer_8 (.in0(Q1), .in1(B0), .out(multiplexer_8_out), .sel(Load));  // open: en
  D_Flip_Flop d_ff_8 (.clk(Clock), .D(multiplexer_8_out), .Q(Q0), .en(Enable));  // open: Qn, preset, reset
endmodule
