// Logisim project case 00.circ as structural Verilog: 1 circuit, main circuit main
module main (
  input  Enable,
  input  A7,
  input  A6,
  input  A5,
  input  A4,
  input  A3,
  input  A2,
  input  A1,
  input  A0,
  input  A8,
  input  A9,
  input  A10,
  input  A11,
  input  A12,
  input  A13,
  input  A14,
  input  A15,
  output Q0,
  output Q1,
  output Q2,
  output Q3,
  output Q4,
  output Q5,
  output Q6,
  output Q7,
  output Q8,
  output Q9,
  output Q10,
  output Q11,
  output Q12,
  output Q13,
  output Q14,
  output Q15
);

  wire not_1_out, not_2_out, not_3_out, not_4_out, not_5_out, not_6_out, not_7_out, not_8_out;

  not not_1 (not_1_out, A8);
  not not_2 (not_2_out, A9);
  not not_3 (not_3_out, A10);
  not not_4 (not_4_out, A11);
  not not_5 (not_5_out, A12);
  not not_6 (not_6_out, A13);
  not not_7 (not_7_out, A14);
  not not_8 (not_8_out, A15);
  and and_1 (Q0, not_1_out, Enable);
  and and_2 (Q1, not_2_out, Enable);
  and and_3 (Q2, not_3_out, Enable);
  and and_4 (Q3, not_4_out, Enable);
  and and_5 (Q4, not_5_out, Enable);
  and and_6 (Q5, not_6_out, Enable);
  and and_7 (Q6, not_7_out, Enable);
  and and_8 (Q7, not_8_out, Enable);

  assign Q8 = 1'b0;
  assign Q9 = 1'b0;
  assign Q10 = 1'b0;
  assign Q11 = 1'b0;
  assign Q12 = 1'b0;
  assign Q13 = 1'b0;
  assign Q14 = 1'b0;
  assign Q15 = 1'b0;
endmodule
