// Logisim project case 01.circ as structural Verilog: 2 circuits, main circuit main
module main (
  input  Enable,
  input  counter_Holder_H,
  input  Clock,
  output Q0,
  output Q1,
  output Q2,
  output Q3,
  output Q4,
  output Q5,
  output Q6,
  output Q7,
  output Q8,
  output Q9,
  output Q10,
  output Q11,
  output Q12,
  output Q13,
  output Q14,
  output Q15
);

  wire and_1_out, modulo_16_down_counter_1_out_7, not_1_out;

  not not_1 (not_1_out, counter_Holder_H);
  and and_1 (and_1_out, Enable, not_1_out);
  Modulo_16_down_counter modulo_16_down_counter_1 (
    .Enable(and_1_out), .Clock(Clock), .out_3(Q11), .out_4(Q10), .out_5(Q9), .out_6(Q8),
    .out_7(modulo_16_down_counter_1_out_7));
  Modulo_16_down_counter modulo_16_down_counter_2 (
    .Enable(modulo_16_down_counter_1_out_7), .Clock(Clock), .out_3(Q15), .out_4(Q14), .out_5(Q13), .out_6(Q12));  // open: out_7

  assign Q0 = 1'b0;
  assign Q1 = 1'b0;
  assign Q2 = 1'b0;
  assign Q3 = 1'b0;
  assign Q4 = 1'b0;
  assign Q5 = 1'b0;
  assign Q6 = 1'b0;
  assign Q7 = 1'b0;
endmodule

// mod16DnCounter
module Modulo_16_down_counter (
  input  Enable,
  input  Clock,
  output out_3,
  output out_4,
  output out_5,
  output out_6,
  output out_7
);

  wire and_1_out, and_2_out, and_3_out, and_4_out, and_5_out, and_6_out, and_7_out, d_ff_1_qn, d_ff_2_qn,
       d_ff_3_qn, d_ff_4_qn, or_1_out, or_2_out, or_3_out, or_4_out;

  or or_1 (or_1_out, out_4, out_5, out_6);
  and and_1 (and_1_out, d_ff_1_qn, d_ff_2_qn, d_ff_3_qn, d_ff_4_qn);
  and and_2 (and_2_out, out_3, or_1_out);
  and and_3 (and_3_out, d_ff_2_qn, d_ff_3_qn, d_ff_4_qn);
  and and_4 (and_4_out, out_4, out_5);
  and and_5 (and_5_out, out_4, out_6);
  and and_6 (and_6_out, out_5, out_6);
  and and_7 (and_7_out, d_ff_3_qn, d_ff_4_qn);
  or or_2 (or_2_out, and_1_out, and_2_out);
  or or_3 (or_3_out, and_3_out, and_4_out, and_5_out);
  or or_4 (or_4_out, and_6_out, and_7_out);
  D_Flip_Flop d_ff_1 (.clk(Clock), .D(or_2_out), .Q(out_3), .Qn(d_ff_1_qn), .en(Enable));  // open: preset, reset
  D_Flip_Flop d_ff_2 (.clk(Clock), .D(or_3_out), .Q(out_4), .Qn(d_ff_2_qn), .en(Enable));  // open: preset, reset
  D_Flip_Flop d_ff_3 (.clk(Clock), .D(or_4_out), .Q(out_5), .Qn(d_ff_3_qn), .en(Enable));  // open: preset, reset
  D_Flip_Flop d_ff_4 (.clk(Clock), .D(d_ff_4_qn), .Q(out_6), .Qn(d_ff_4_qn), .en(Enable));  // open: preset, reset
  and and_8 (out_7, Enable, or_2_out, or_3_out, or_4_out, d_ff_4_qn);

  // Notes on the sheet:
  //   A
  //   C
  //   B
  //   D
endmodule
