// Logisim project case 10.circ as structural Verilog: 1 circuit, main circuit main
module main (
  input  A0,
  input  A1,
  input  A2,
  input  A3,
  input  A4,
  input  A5,
  input  A6,
  input  A7,
  input  A8,
  input  A9,
  input  A10,
  input  A11,
  input  A12,
  input  A13,
  input  A14,
  input  A15,
  input  Clock,
  input  Enable,
  input  B0,
  input  B1,
  input  B2,
  input  Load,
  input  B3,
  input  B4,
  input  B5,
  input  B6,
  input  B7,
  output Q0,
  output Q1,
  output Q2,
  output Q3,
  output Q4,
  output Q5,
  output Q6,
  output Q7,
  output Q8,
  output Q9,
  output Q10,
  output Q11,
  output Q12,
  output Q13,
  output Q14,
  output Q15
);

  wire main_2_q0, main_2_q1, main_2_q2, main_2_q3, main_2_q4, main_2_q5, main_2_q6, main_2_q7, main_2_q8,
       main_2_q9, main_2_q10, main_2_q11, main_2_q12, main_2_q13, main_2_q14, main_2_q15, main_4_q0,
       undriven, undriven_2, undriven_3, undriven_4, undriven_5, undriven_6, undriven_7, undriven_8,
       undriven_9, undriven_10, undriven_11, undriven_12, undriven_13, undriven_14, undriven_15, undriven_16;

  // SL_main main_1: pin names not known; wires that end beside it: A0, A1, A2, A3, A4, A5, A6, A7, A8, A9, A10, A11, A12, A13, A14, A15, Enable, Clock, Load
  full_adder_main main_2 (
    .B15(undriven_11), .A15(Q15), .B14(undriven_10), .A14(Q14), .B13(undriven_12), .A13(Q13),
    .B12(undriven_9), .A12(Q12), .B11(undriven_8), .A11(Q11), .B10(undriven_7), .A10(Q10), .B9(undriven_6),
    .A9(Q9), .B8(undriven_13), .A8(Q8), .B7(undriven_5), .A7(Q7), .B6(undriven_4), .A6(Q6), .B5(undriven_14),
    .A5(Q5), .B4(undriven_15), .A4(Q4), .B3(undriven_3), .A3(Q3), .B2(undriven_2), .A2(Q2), .B1(undriven_16),
    .A1(Q1), .Cin(1'b0), .B0(undriven), .A0(Q0), .Q15(main_2_q15), .Q14(main_2_q14), .Q13(main_2_q13),
    .Q11(main_2_q11), .Q10(main_2_q10), .Q9(main_2_q9), .Q8(main_2_q8), .Q7(main_2_q7), .Q6(main_2_q6),
    .Q5(main_2_q5), .Q4(main_2_q4), .Q3(main_2_q3), .Q2(main_2_q2), .Q1(main_2_q1), .Q0(main_2_q0),
    .Q12(main_2_q12), .Enable(main_4_q0));  // open: Cout
  Product_main main_3 (
    .Enable(Enable), .A15(main_2_q15), .A14(main_2_q14), .A13(main_2_q13), .A12(main_2_q12),
    .A11(main_2_q11), .A10(main_2_q10), .A9(main_2_q9), .A8(main_2_q8), .A7(main_2_q7), .A6(main_2_q6),
    .A5(main_2_q5), .A4(main_2_q4), .A3(main_2_q3), .A2(main_2_q2), .A1(main_2_q1), .A0(main_2_q0),
    .Q15(Q15), .Q14(Q14), .Q13(Q13), .Q12(Q12), .Q11(Q11), .Q10(Q10), .Q9(Q9), .Q8(Q8), .Q7(Q7), .Q6(Q6),
    .Q5(Q5), .Q4(Q4), .Q3(Q3), .Q2(Q2), .Q1(Q1), .Q0(Q0), .Clock(Clock), .Load(main_4_q0), .Reset(Load));
  SR_main main_4 (
    .Load(Load), .Enable(Enable), .B7(B7), .B6(B6), .B5(B5), .B4(B4), .B3(B3), .B2(B2), .B1(B1), .B0(B0),
    .Q0(main_4_q0), .Clock(Clock));  // open: Q7, Q6, Q5, Q4, Q3, Q2, Q1
endmodule
