// Logisim project full adder.circ as structural Verilog: 1 circuit, main circuit main
module main (
  input  B3,
  input  A3,
  input  B2,
  input  A2,
  input  B1,
  input  A1,
  input  B11,
  input  A11,
  input  B10,
  input  A10,
  input  B9,
  input  A9,
  input  B0,
  input  A0,
  input  B8,
  input  A8,
  input  B7,
  input  A7,
  input  B6,
  input  A6,
  input  B5,
  input  A5,
  input  B15,
  input  A15,
  input  B14,
  input  A14,
  input  B13,
  input  A13,
  input  B4,
  input  A4,
  input  B12,
  input  A12,
  input  Cin,
  input  Enable,
  output Cout,
  output Q13,
  output Q14,
  output Q12,
  output Q11,
  output Q8,
  output Q6,
  output Q10,
  output Q7,
  output Q15,
  output Q9,
  output Q5,
  output Q4,
  output Q3,
  output Q0,
  output Q1,
  output Q2
);

  wire and_1_out, and_2_out, and_4_out, and_5_out, and_7_out, and_8_out, and_10_out, and_11_out, and_13_out,
       and_14_out, and_16_out, and_17_out, and_19_out, and_20_out, and_22_out, and_23_out, and_25_out,
       and_26_out, and_28_out, and_29_out, and_31_out, and_32_out, and_34_out, and_35_out, and_37_out,
       and_38_out, and_40_out, and_41_out, and_43_out, and_44_out, and_46_out, and_47_out, or_2_out,
       or_3_out, or_4_out, or_5_out, or_6_out, or_7_out, or_8_out, or_9_out, or_10_out, or_11_out, or_12_out,
       or_13_out, or_14_out, or_15_out, or_16_out, xor_1_out, xor_2_out, xor_3_out, xor_4_out, xor_5_out,
       xor_6_out, xor_7_out, xor_8_out, xor_9_out, xor_10_out, xor_11_out, xor_12_out, xor_13_out,
       xor_14_out, xor_15_out, xor_16_out, xor_17_out, xor_18_out, xor_19_out, xor_20_out, xor_21_out,
       xor_22_out, xor_23_out, xor_24_out, xor_25_out, xor_26_out, xor_27_out, xor_28_out, xor_29_out,
       xor_30_out, xor_31_out, xor_32_out;

  and and_1 (and_1_out, xor_1_out, or_2_out);
  or or_1 (Cout, and_1_out, and_2_out);
  and and_2 (and_2_out, B15, A15);
  xor xor_1 (xor_1_out, B15, A15);
  xor xor_2 (xor_2_out, or_2_out, xor_1_out);
  and and_3 (Q15, xor_2_out, Enable);
  and and_4 (and_4_out, xor_3_out, or_3_out);
  and and_5 (and_5_out, B14, A14);
  or or_2 (or_2_out, and_4_out, and_5_out);
  xor xor_3 (xor_3_out, B14, A14);
  xor xor_4 (xor_4_out, or_3_out, xor_3_out);
  and and_6 (Q14, xor_4_out, Enable);
  and and_7 (and_7_out, xor_6_out, or_4_out);
  and and_8 (and_8_out, B13, A13);
  or or_3 (or_3_out, and_7_out, and_8_out);
  xor xor_5 (xor_5_out, or_4_out, xor_6_out);
  and and_9 (Q13, xor_5_out, Enable);
  xor xor_6 (xor_6_out, B13, A13);
  and and_10 (and_10_out, xor_8_out, or_5_out);
  and and_11 (and_11_out, A12, B12);
  or or_4 (or_4_out, and_10_out, and_11_out);
  xor xor_7 (xor_7_out, or_5_out, xor_8_out);
  and and_12 (Q12, xor_7_out, Enable);
  xor xor_8 (xor_8_out, B12, A12);
  and and_13 (and_13_out, xor_9_out, or_6_out);
  or or_5 (or_5_out, and_13_out, and_14_out);
  and and_14 (and_14_out, B11, A11);
  xor xor_9 (xor_9_out, B11, A11);
  xor xor_10 (xor_10_out, or_6_out, xor_9_out);
  and and_15 (Q11, xor_10_out, Enable);
  and and_16 (and_16_out, xor_11_out, or_7_out);
  and and_17 (and_17_out, B10, A10);
  or or_6 (or_6_out, and_16_out, and_17_out);
  xor xor_11 (xor_11_out, B10, A10);
  xor xor_12 (xor_12_out, or_7_out, xor_11_out);
  and and_18 (Q10, xor_12_out, Enable);
  and and_19 (and_19_out, xor_14_out, or_8_out);
  and and_20 (and_20_out, B9, A9);
  or or_7 (or_7_out, and_19_out, and_20_out);
  xor xor_13 (xor_13_out, or_8_out, xor_14_out);
  and and_21 (Q9, xor_13_out, Enable);
  xor xor_14 (xor_14_out, B9, A9);
  and and_22 (and_22_out, xor_16_out, or_9_out);
  and and_23 (and_23_out, A8, B8);
  or or_8 (or_8_out, and_22_out, and_23_out);
  xor xor_15 (xor_15_out, or_9_out, xor_16_out);
  and and_24 (Q8, xor_15_out, Enable);
  xor xor_16 (xor_16_out, B8, A8);
  and and_25 (and_25_out, xor_17_out, or_10_out);
  or or_9 (or_9_out, and_25_out, and_26_out);
  and and_26 (and_26_out, B7, A7);
  xor xor_17 (xor_17_out, B7, A7);
  xor xor_18 (xor_18_out, or_10_out, xor_17_out);
  and and_27 (Q7, xor_18_out, Enable);
  and and_28 (and_28_out, xor_19_out, or_11_out);
  and and_29 (and_29_out, B6, A6);
  or or_10 (or_10_out, and_28_out, and_29_out);
  xor xor_19 (xor_19_out, B6, A6);
  xor xor_20 (xor_20_out, or_11_out, xor_19_out);
  and and_30 (Q6, xor_20_out, Enable);
  and and_31 (and_31_out, xor_22_out, or_12_out);
  and and_32 (and_32_out, B5, A5);
  or or_11 (or_11_out, and_31_out, and_32_out);
  xor xor_21 (xor_21_out, or_12_out, xor_22_out);
  and and_33 (Q5, xor_21_out, Enable);
  xor xor_22 (xor_22_out, B5, A5);
  and and_34 (and_34_out, xor_24_out, or_13_out);
  and and_35 (and_35_out, A4, B4);
  or or_12 (or_12_out, and_34_out, and_35_out);
  xor xor_23 (xor_23_out, or_13_out, xor_24_out);
  and and_36 (Q4, xor_23_out, Enable);
  xor xor_24 (xor_24_out, B4, A4);
  and and_37 (and_37_out, xor_25_out, or_14_out);
  or or_13 (or_13_out, and_37_out, and_38_out);
  and and_38 (and_38_out, B3, A3);
  xor xor_25 (xor_25_out, B3, A3);
  xor xor_26 (xor_26_out, or_14_out, xor_25_out);
  and and_39 (Q3, xor_26_out, Enable);
  and and_40 (and_40_out, xor_27_out, or_15_out);
  and and_41 (and_41_out, B2, A2);
  or or_14 (or_14_out, and_40_out, and_41_out);
  xor xor_27 (xor_27_out, B2, A2);
  xor xor_28 (xor_28_out, or_15_out, xor_27_out);
  and and_42 (Q2, xor_28_out, Enable);
  and and_43 (and_43_out, xor_30_out, or_16_out);
  and and_44 (and_44_out, B1, A1);
  or or_15 (or_15_out, and_43_out, and_44_out);
  xor xor_29 (xor_29_out, or_16_out, xor_30_out);
  and and_45 (Q1, xor_29_out, Enable);
  xor xor_30 (xor_30_out, B1, A1);
  and and_46 (and_46_out, xor_32_out, Cin);
  and and_47 (and_47_out, A0, B0);
  or or_16 (or_16_out, and_46_out, and_47_out);
  xor xor_31 (xor_31_out, Cin, xor_32_out);
  and and_48 (Q0, xor_31_out, Enable);
  xor xor_32 (xor_32_out, B0, A0);
endmodule
